# Fritzing sketch Hardware (saved by Fritzing 0.9.3b)

parts:
  DC_Mot_Enc1 = DC Motor with two-phase hall-encoder [part_number=VT-E-G25A-06-177E]
  부품1 = Arduino Motor Shield (Rev3)

nets:
  N1: DC_Mot_Enc1.pin1, 부품1.A+
  N2: DC_Mot_Enc1.pin2, 부품1.A-
  N3: DC_Mot_Enc1.pin3, 부품1.D2
  N4: DC_Mot_Enc1.pin4, 부품1.D3_PWM/A
  N5: DC_Mot_Enc1.pin5, 부품1.GND
  N6: DC_Mot_Enc1.pin6, 부품1.5V
